# Fritzing sketch capitulo3 (saved by Fritzing 0.9.3b)
breadboards: 1

parts:
  Part1 = Arduino Uno (Rev3)
  LED3 = LED - 5mm [color="Red (633nm)" package="5 mm [THT]"]
  R3 = Resistor [tolerance=±5% resistance=220 package=THT]
  S5 = Momentary Switch [package=ksa_sealed_tac_switch]
  R4 = Resistor [tolerance=±5% resistance=220 package=THT]
  LED4 = LED - 5mm [color="Red (633nm)" package="5 mm [THT]"]
  S6 = Momentary Switch [package=ksa_sealed_tac_switch]
  R5 = Resistor [tolerance=±5% resistance=220 package=THT]
  LED5 = LED - 5mm [color="Red (633nm)" package="5 mm [THT]"]
  S7 = Momentary Switch [package=ksa_sealed_tac_switch]
  R6 = Resistor [tolerance=±5% resistance=220 package=THT]
  LED6 = LED - 5mm [color="Red (633nm)" package="5 mm [THT]"]
  S8 = Momentary Switch [package=ksa_sealed_tac_switch]

nets:
  N1: Part1.D10_PWM/SS, S5.1, S5.2
  N2: Part1.D11_PWM/MOSI, S6.1, S6.2
  N3: Part1.D12/MISO, S7.1, S7.2
  N4: Part1.D13/SCK, S8.1, S8.2
  N5: Part1.GND, R3.Pin_0, S5.3, S5.4, R4.Pin_0, R5.Pin_0, R6.Pin_0
  N6: Part1.D2, LED3.anode
  N7: Part1.D3_PWM, LED4.anode
  N8: Part1.D4, LED5.anode
  N9: Part1.D5_PWM, LED6.anode
  N10: LED3.cathode, R3.Pin_1
  N11: R4.Pin_1, LED4.cathode
  N12: S6.3, S6.4
  N13: R5.Pin_1, LED5.cathode
  N14: S7.3, S7.4
  N15: R6.Pin_1, LED6.cathode
  N16: S8.3, S8.4
