# Fritzing sketch capitulo8 (saved by Fritzing 0.9.3b)
breadboards: 1

parts:
  Part1 = Arduino Uno (Rev3)
  S1 = Momentary Switch [package=ksa_sealed_tac_switch]
  LED3 = LED - 5mm [color="Red (633nm)" package="5 mm [THT]"]
  R3 = Resistor [tolerance=±5% resistance=220 package=THT]
  R4 = Resistor [tolerance=±5% resistance=220 package=THT]
  LED4 = LED - 5mm [color="Red (633nm)" package="5 mm [THT]"]  # not connected
  S2 = Momentary Switch [package=ksa_sealed_tac_switch]  # not connected
  R5 = Resistor [tolerance=±5% resistance=220 package=THT]  # not connected
  LED5 = LED - 5mm [color="Red (633nm)" package="5 mm [THT]"]
  S3 = Momentary Switch [package=ksa_sealed_tac_switch]
  R6 = Resistor [tolerance=±5% resistance=220 package=THT]
  LED6 = LED - 5mm [color="Red (633nm)" package="5 mm [THT]"]
  S4 = Momentary Switch [package=ksa_sealed_tac_switch]
  U1 = POT [package=pot_alpha_rv16af-20]

nets:
  N1: Part1.A0, U1.S
  N2: Part1.D8, S1.3
  N3: Part1.D10_PWM/SS, S3.3
  N4: Part1.D11_PWM/MOSI, S4.3
  N5: Part1.D2, LED3.anode
  N6: Part1.D4, LED5.anode
  N7: Part1.D5_PWM, LED6.anode
  N8: Part1.5V, U1.E
  N9: Part1.GND, S1.2, R3.Pin_1, R4.Pin_1, S3.2, R6.Pin_1, S4.2, U1.A
  N10: LED3.cathode, R3.Pin_0
  N11: R6.Pin_0, LED6.cathode
